// Logisim project Real_Alu-Gabri-salvo.circ as structural Verilog
module A_And_B (
  input  [7:0] A,
  input  [7:0] B,
  output [7:0] out_3,
  output out_4
);

  assign out_3 = A & B;  // AND_Gate and_1, 8 bits wide
  FLAG_Z flag_z_1 (.in_1(out_3), .out_2(out_4));
endmodule

module in_A_OR_in_B (
  input  [7:0] A,
  input  [7:0] B,
  output [7:0] out_3,
  output out_4
);

  assign out_3 = A | B;  // OR_Gate or_1, 8 bits wide
  FLAG_Z flag_z_1 (.in_1(out_3), .out_2(out_4));
endmodule

module Full_adder (
  input  C0,
  input  a,
  input  b,
  output S,
  output C1
);

  wire and_1_out, and_2_out, and_3_out, xor_1_out;

  xor xor_1 (xor_1_out, a, b);
  and and_1 (and_1_out, C0, a);
  and and_2 (and_2_out, a, b);
  and and_3 (and_3_out, C0, b);
  xor xor_2 (S, xor_1_out, C0);
  or or_1 (C1, and_1_out, and_2_out, and_3_out);
endmodule

module adder_4_bit (
  input  c0,
  input  a0,
  input  b0,
  input  a1,
  input  b1,
  input  a2,
  input  b2,
  input  a3,
  input  b3,
  output s0,
  output s1,
  output s2,
  output s3,
  output C
);

  wire full_adder_1_c1, full_adder_2_c1, full_adder_3_c1;

  Full_adder full_adder_1 (.S(s0), .C1(full_adder_1_c1), .C0(c0), .a(a0), .b(b0));
  Full_adder full_adder_2 (.S(s1), .C1(full_adder_2_c1), .C0(full_adder_1_c1), .a(a1), .b(b1));
  Full_adder full_adder_3 (.S(s2), .C1(full_adder_3_c1), .C0(full_adder_2_c1), .a(a2), .b(b2));
  Full_adder full_adder_4 (.S(s3), .C1(C), .C0(full_adder_3_c1), .a(a3), .b(b3));
endmodule

module Adder_8_Bits (
  input  a7,
  input  b7,
  input  a6,
  input  b6,
  input  a5,
  input  b5,
  input  a4,
  input  b4,
  input  a3,
  input  b3,
  input  a2,
  input  b2,
  input  a1,
  input  b1,
  input  a0,
  input  b0,
  input  in_17,
  output overflow,
  output s7,
  output s6,
  output s5,
  output s4,
  output s3,
  output s2,
  output s1,
  output s0
);

  wire adder_4_bit_2_c;

  adder_4_bit adder_4_bit_1 (
    .s0(s4), .s1(s5), .s2(s6), .s3(s7), .a0(a4), .a1(a5), .a2(a6), .a3(a7), .b0(b4), .b1(b5), .b2(b6),
    .b3(b7), .c0(adder_4_bit_2_c), .C(overflow));
  adder_4_bit adder_4_bit_2 (
    .s0(s0), .s1(s1), .s2(s2), .s3(s3), .a0(a0), .a1(a1), .a2(a2), .a3(a3), .b0(b0), .b1(b1), .b2(b2),
    .b3(b3), .c0(in_17), .C(adder_4_bit_2_c));
endmodule

module CPL2 (
  input  [7:0] in_1,
  output C,
  output [7:0] out_3
);

  wire halfadder_1_c, halfadder_2_c, halfadder_3_c, halfadder_4_c, halfadder_5_c, halfadder_6_c,
       halfadder_8_c;
  wire [7:0] not_1_out;

  assign not_1_out = ~in_1;  // NOT_Gate not_1, 8 bits wide
  Halfadder halfadder_1 (.a(not_1_out[1]), .b(halfadder_2_c), .S(out_3[1]), .C(halfadder_1_c));
  Halfadder halfadder_2 (.a(1'b1), .b(not_1_out[0]), .S(out_3[0]), .C(halfadder_2_c));
  Halfadder halfadder_3 (.a(not_1_out[3]), .b(halfadder_4_c), .S(out_3[3]), .C(halfadder_3_c));
  Halfadder halfadder_4 (.a(not_1_out[2]), .b(halfadder_1_c), .S(out_3[2]), .C(halfadder_4_c));
  Halfadder halfadder_5 (.a(not_1_out[5]), .b(halfadder_6_c), .S(out_3[5]), .C(halfadder_5_c));
  Halfadder halfadder_6 (.a(not_1_out[4]), .b(halfadder_3_c), .S(out_3[4]), .C(halfadder_6_c));
  Halfadder halfadder_7 (.a(not_1_out[7]), .b(halfadder_8_c), .S(out_3[7]), .C(C));
  Halfadder halfadder_8 (.a(not_1_out[6]), .b(halfadder_5_c), .S(out_3[6]), .C(halfadder_8_c));
endmodule

module Halfadder (
  input  a,
  input  b,
  output S,
  output C
);

  and and_1 (C, a, b);
  xor xor_1 (S, a, b);
endmodule

module NOT_in_B (
  input  [7:0] B,
  output [7:0] NOT_B,
  output out_3
);

  assign NOT_B = ~B;  // NOT_Gate not_1, 8 bits wide
  FLAG_Z flag_z_1 (.in_1(NOT_B), .out_2(out_3));
endmodule

module Sottrattore_8_bits (
  input  [7:0] B,
  input  [7:0] A,
  input  in_3,
  output out_4,
  output [7:0] out_5
);

  wire cpl2_1_c;
  wire [7:0] cpl2_1_out_3;

  Adder_8_Bits adder_8_bits_1 (
    .a7(A[7]), .a6(A[6]), .a5(A[5]), .a4(A[4]), .a3(A[3]), .a2(A[2]), .a1(A[1]), .a0(A[0]),
    .b7(cpl2_1_out_3[7]), .b6(cpl2_1_out_3[6]), .b5(cpl2_1_out_3[5]), .b4(cpl2_1_out_3[4]),
    .b3(cpl2_1_out_3[3]), .b2(cpl2_1_out_3[2]), .b1(cpl2_1_out_3[1]), .b0(cpl2_1_out_3[0]), .in_17(in_3),
    .overflow(out_4), .s7(out_5[7]), .s6(out_5[6]), .s5(out_5[5]), .s4(out_5[4]), .s3(out_5[3]),
    .s2(out_5[2]), .s1(out_5[1]), .s0(out_5[0]));
  CPL2 cpl2_1 (.in_1(B), .C(cpl2_1_c), .out_3(cpl2_1_out_3));
  LED led_1 (.in(cpl2_1_c));
  // Probe on cpl2_1_out_3
endmodule

module Incremento (
  input  [7:0] A,
  input  in_2,
  output out_3,
  output [7:0] out_4
);

  Adder_8_Bits adder_8_bits_1 (
    .a7(A[7]), .a6(A[6]), .a5(A[5]), .a4(A[4]), .a3(A[3]), .a2(A[2]), .a1(A[1]), .a0(A[0]), .b7(1'b0),
    .b6(1'b0), .b5(1'b0), .b4(1'b0), .b3(1'b0), .b2(1'b0), .b1(1'b0), .b0(1'b1), .in_17(in_2),
    .overflow(out_3), .s7(out_4[7]), .s6(out_4[6]), .s5(out_4[5]), .s4(out_4[4]), .s3(out_4[3]),
    .s2(out_4[2]), .s1(out_4[1]), .s0(out_4[0]));
endmodule

module Decrementatore (
  input  in_1,
  input  [7:0] A,
  output [7:0] out_3,
  output out_4
);

  Sottrattore_8_bits sottrattore_8_bits_1 (.B(8'h1), .A(A), .out_5(out_3), .in_3(in_1), .out_4(out_4));
endmodule

module LSL (
  input  [7:0] B,
  output out_2,
  output out_3,
  output [7:0] out_4,
  output out_5
);

  FLAG_N flag_n_1 (.in_1({B[6:0], 1'b0}), .out_2(out_2));
  FLAG_Z flag_z_1 (.in_1({B[6:0], 1'b0}), .out_2(out_5));

  assign out_3 = B[7];
  assign out_4 = {B[6:0], 1'b0};
endmodule

module LSR (
  input  [7:0] B,
  output out_2,
  output out_3,
  output [7:0] out_4,
  output out_5
);

  FLAG_N flag_n_1 (.in_1({1'b0, B[7:1]}), .out_2(out_2));
  FLAG_Z flag_z_1 (.in_1({1'b0, B[7:1]}), .out_2(out_5));

  assign out_3 = B[0];
  assign out_4 = {1'b0, B[7:1]};
endmodule

module FLAG_Z (
  input  [7:0] in_1,
  output out_2
);

  nor nor_1 (out_2, in_1[0], in_1[1], in_1[2], in_1[3], in_1[4], in_1[5], in_1[6], in_1[7]);
endmodule

module FLAG_N (
  input  [7:0] in_1,
  output out_2
);


  assign out_2 = in_1[7];
endmodule

module MUX_da_2_a_1 (
  input  in_1,
  input  in_2,
  input  in_3,
  output out_4
);

  wire and_1_out, and_2_out, not_1_out;

  not not_1 (not_1_out, in_1);
  and and_1 (and_1_out, not_1_out, in_2);
  and and_2 (and_2_out, in_1, in_3);
  or or_1 (out_4, and_1_out, and_2_out);
endmodule

module MUX_da_4_a_1 (
  input  in_1,
  input  in_2,
  input  in_3,
  input  in_4,
  input  in_5,
  input  in_6,
  output out_7
);

  wire and_1_out, and_2_out, and_3_out, and_4_out, not_1_out, not_2_out;

  not not_1 (not_1_out, in_1);
  not not_2 (not_2_out, in_2);
  and and_1 (and_1_out, not_1_out, not_2_out, in_3);
  and and_2 (and_2_out, not_1_out, in_2, in_4);
  and and_3 (and_3_out, in_1, not_2_out, in_5);
  and and_4 (and_4_out, in_1, in_2, in_6);
  or or_1 (out_7, and_1_out, and_2_out, and_3_out, and_4_out);
endmodule

module Mux_da_8_a_1 (
  input  s1,
  input  s0,
  input  S,
  input  in_4,
  input  in_5,
  input  in_6,
  input  in_7,
  input  in_8,
  input  in_9,
  input  in_10,
  input  in_11,
  output out_12
);

  wire mux_da_4_a_1_1_out_7, mux_da_4_a_1_2_out_7;

  MUX_da_4_a_1 mux_da_4_a_1_1 (
    .in_3(in_4), .in_4(in_5), .in_5(in_6), .in_6(in_7), .out_7(mux_da_4_a_1_1_out_7), .in_1(s1), .in_2(s0));
  MUX_da_4_a_1 mux_da_4_a_1_2 (
    .in_3(in_8), .in_4(in_9), .in_5(in_10), .in_6(in_11), .out_7(mux_da_4_a_1_2_out_7), .in_1(s1), .in_2(s0));
  MUX_da_2_a_1 mux_da_2_a_1_1 (.in_2(mux_da_4_a_1_1_out_7), .in_3(mux_da_4_a_1_2_out_7), .out_4(out_12), .in_1(S));
endmodule
